# Fritzing sketch ExFarm (saved by Fritzing 0.9.3b)
breadboards: 1

parts:
  パーツ1 = Arduino Pro Mini v13
  パーツ2 = Real Time Clock Module - DS1307 RTC Breakout Board
  パーツ3 = Soil Moisture Sensor
  KY-1 = Keyes Relay [package=THT]
  J1 = Piezo Speaker

nets:
  VCC: パーツ1.VCC, パーツ2.5V, パーツ3.VCC, KY-1.power
  GND: パーツ1.GND, パーツ2.GND, パーツ3.GND, KY-1.ground, J1.pin1
  N1: パーツ1.A4, パーツ2.SDA
  N2: パーツ1.A5, パーツ2.SCL
  N3: パーツ1.RAW, KY-1.C
  N4: パーツ1.A0, パーツ3.SIG
  N5: パーツ1.D4, J1.pin2
  N6: パーツ1.D3_PWM, KY-1.signal
  N7: パーツ1.D2, パーツ2.SQW

notes:
  [WatorPump]
  ・＋[黄]
  ・ー[青]
  ・Sig(On/Off)[緑]
  ※Sigは5V以上必要
  [電池]8V
  ・＋
  ・ー
  #define DEBUG_PIN 11 // デバッグモードピン 起動時にGNDと接続でデバッグモードで起動。割り込み毎分・水やり間隔２分
  #define DATA_CLEAR_PIN 12 // データ消去ピン 起動時にGNDと接続でデータの書き込み位置を初期化

custom parts:
  Keyes Relay: The Keyes 5V relay module is suitable for SCM development, home appliance control. It uses a 5V~12V TIL control signal which can control DC / AC signal.
